// Logisim project logic_gates.circ as structural Verilog: 1 circuit, main circuit main
module main (
  input  A,
  input  B,
  output And,
  output OR,
  output Not
);

  and and_1 (And, A, B);
  or or_1 (OR, A, B);
  not not_1 (Not, A);
endmodule
