// Logisim project 6.2_1.circ as structural Verilog: 1 circuit, main circuit main
module main (
  input  [3:0] S0,
  input  [3:0] S1,
  input  [3:0] D0,
  input  [3:0] D1,
  input  [3:0] D2,
  input  [3:0] D3,
  output [3:0] Y
);

  wire [3:0] and_1_out, and_2_out, and_3_out, and_4_out, not_1_out, not_2_out;

  assign not_1_out = ~S0;  // NOT_Gate not_1, 4 bits wide
  assign not_2_out = ~S1;  // NOT_Gate not_2, 4 bits wide
  assign and_1_out = D0 & not_2_out & not_1_out;  // AND_Gate and_1, 4 bits wide
  assign and_2_out = D1 & not_2_out & S0;  // AND_Gate and_2, 4 bits wide
  assign and_3_out = D2 & S1 & not_1_out;  // AND_Gate and_3, 4 bits wide
  assign and_4_out = D3 & S1 & S0;  // AND_Gate and_4, 4 bits wide
  assign Y = and_1_out | and_2_out | and_3_out | and_4_out;  // OR_Gate or_1, 4 bits wide

  // Notes on the sheet:
  //   ~S0
  //   ~S1
endmodule
