// Logisim project 6.2_2.circ as structural Verilog: 1 circuit, main circuit main
module main (
  input  C,
  input  S2,
  input  S1,
  output Z0,
  output Z1,
  output Z2,
  output Z3
);

  wire and_1_out, and_2_out, and_3_out, and_4_out, not_1_out, not_2_out, not_3_out, not_4_out;

  not not_1 (not_1_out, S1);
  not not_2 (not_2_out, S2);
  not not_3 (not_3_out, S1);
  not not_4 (not_4_out, S2);
  and and_1 (and_1_out, S1, S2);
  and and_2 (and_2_out, not_1_out, not_2_out);
  and and_3 (and_3_out, not_3_out, S2);
  and and_4 (and_4_out, S1, not_4_out);
  and and_5 (Z3, and_1_out, C);
  and and_6 (Z0, and_2_out, C);
  and and_7 (Z1, and_3_out, C);
  and and_8 (Z2, and_4_out, C);
endmodule
