// Logisim project 6.2_3.circ as structural Verilog: 1 circuit, main circuit main
module main (
  input  D0,
  input  D1,
  input  D2,
  input  D3,
  input  D4,
  input  D5,
  input  D6,
  input  D7,
  input  [2:0] ABC,
  output f0,
  output f1,
  output f2,
  output f3,
  output f4,
  output f5,
  output f6,
  output f7
);

  wire multiplexer_1_out;

  Multiplexer #(.select(3)) multiplexer_1 (
    .in0(D0), .in1(D1), .in2(D2), .in3(D3), .in4(D4), .in5(D5), .in6(D6), .in7(D7), .out(multiplexer_1_out),
    .sel(ABC));
  Demultiplexer #(.select(3)) demultiplexer_1 (
    .out0(f0), .out1(f1), .out2(f2), .out3(f3), .out4(f4), .out5(f5), .out6(f6), .out7(f7),
    .in(multiplexer_1_out), .sel(ABC));
endmodule
