// Logisim project 6.7_1.circ as structural Verilog: 1 circuit, main circuit main
module main (
  input  T1,
  output Q0,
  output Q1,
  output [2:0] out_4,
  output Q2,
  output C
);

  wire and_1_out, clock_1_out;

  Clock clock_1 (.out(clock_1_out));
  and and_1 (and_1_out, out_4[1], out_4[0]);
  J_K_Flip_Flop j_k_ff_1 (.J(T1), .clk(clock_1_out), .K(T1), .Q(out_4[0]));  // open: Qn, preset, reset
  J_K_Flip_Flop j_k_ff_2 (.J(out_4[0]), .clk(clock_1_out), .K(out_4[0]), .Q(out_4[1]));  // open: Qn, preset, reset
  J_K_Flip_Flop j_k_ff_3 (.J(and_1_out), .clk(clock_1_out), .K(and_1_out), .Q(out_4[2]));  // open: Qn, preset, reset
  and and_2 (C, out_4[2], out_4[1], out_4[0]);

  assign Q0 = out_4[0];
  assign Q1 = out_4[1];
  assign Q2 = out_4[2];

  // Notes on the sheet:
  //   CLK
  //   oQ
endmodule
