// Logisim project Regfiles.circ as structural Verilog: 1 circuit, main circuit main
module main (
  input  [3:0] in_1,
  input  we,
  input  [3:0] in_3,
  input  rst,
  input  [3:0] in_5,
  input  [3:0] in_6,
  output [3:0] out_7,
  output [3:0] out_8
);

  wire clock_1_out, demultiplexer_1_out0, demultiplexer_1_out1, demultiplexer_1_out2, demultiplexer_1_out3,
       demultiplexer_1_out4, demultiplexer_1_out5, demultiplexer_1_out6, demultiplexer_1_out7,
       demultiplexer_1_out8, demultiplexer_1_out9, demultiplexer_1_out10, demultiplexer_1_out11,
       demultiplexer_1_out12, demultiplexer_1_out13, demultiplexer_1_out14, demultiplexer_1_out15, not_1_out;
  wire [3:0] register_1_q, register_2_q, register_3_q, register_4_q, register_5_q, register_6_q,
       register_7_q, register_8_q, register_9_q, register_10_q, register_11_q, register_12_q, register_13_q,
       register_14_q, register_15_q, register_16_q;

  Clock clock_1 (.out(clock_1_out));
  Demultiplexer #(.disabled("Z"), .enable("true"), .select(4)) demultiplexer_1 (
    .out0(demultiplexer_1_out0), .out1(demultiplexer_1_out1), .out2(demultiplexer_1_out2),
    .out3(demultiplexer_1_out3), .out4(demultiplexer_1_out4), .out5(demultiplexer_1_out5),
    .out6(demultiplexer_1_out6), .out7(demultiplexer_1_out7), .out8(demultiplexer_1_out8),
    .out9(demultiplexer_1_out9), .out10(demultiplexer_1_out10), .out11(demultiplexer_1_out11),
    .out12(demultiplexer_1_out12), .out13(demultiplexer_1_out13), .out14(demultiplexer_1_out14),
    .out15(demultiplexer_1_out15), .in(1'b1), .sel(in_3), .en(we));
  not not_1 (not_1_out, we);
  Register #(.trigger("falling"), .width(4)) register_1 (
    .D(in_1), .en(demultiplexer_1_out0), .clk(clock_1_out), .Q(register_1_q), .clr(rst));
  Register #(.trigger("falling"), .width(4)) register_2 (
    .D(in_1), .en(demultiplexer_1_out2), .clk(clock_1_out), .Q(register_2_q), .clr(rst));
  Register #(.trigger("falling"), .width(4)) register_3 (
    .D(in_1), .en(demultiplexer_1_out4), .clk(clock_1_out), .Q(register_3_q), .clr(rst));
  Register #(.trigger("falling"), .width(4)) register_4 (
    .D(in_1), .en(demultiplexer_1_out6), .clk(clock_1_out), .Q(register_4_q), .clr(rst));
  Register #(.trigger("falling"), .width(4)) register_5 (
    .D(in_1), .en(demultiplexer_1_out8), .clk(clock_1_out), .Q(register_5_q), .clr(rst));
  Register #(.trigger("falling"), .width(4)) register_6 (
    .D(in_1), .en(demultiplexer_1_out10), .clk(clock_1_out), .Q(register_6_q), .clr(rst));
  Register #(.trigger("falling"), .width(4)) register_7 (
    .D(in_1), .en(demultiplexer_1_out12), .clk(clock_1_out), .Q(register_7_q), .clr(rst));
  Register #(.trigger("falling"), .width(4)) register_8 (
    .D(in_1), .en(demultiplexer_1_out14), .clk(clock_1_out), .Q(register_8_q), .clr(rst));
  Register #(.trigger("falling"), .width(4)) register_9 (
    .D(in_1), .en(demultiplexer_1_out1), .clk(clock_1_out), .Q(register_9_q), .clr(rst));
  Register #(.trigger("falling"), .width(4)) register_10 (
    .D(in_1), .en(demultiplexer_1_out3), .clk(clock_1_out), .Q(register_10_q), .clr(rst));
  Register #(.trigger("falling"), .width(4)) register_11 (
    .D(in_1), .en(demultiplexer_1_out5), .clk(clock_1_out), .Q(register_11_q), .clr(rst));
  Register #(.trigger("falling"), .width(4)) register_12 (
    .D(in_1), .en(demultiplexer_1_out7), .clk(clock_1_out), .Q(register_12_q), .clr(rst));
  Register #(.trigger("falling"), .width(4)) register_13 (
    .D(in_1), .en(demultiplexer_1_out9), .clk(clock_1_out), .Q(register_13_q), .clr(rst));
  Register #(.trigger("falling"), .width(4)) register_14 (
    .D(in_1), .en(demultiplexer_1_out11), .clk(clock_1_out), .Q(register_14_q), .clr(rst));
  Register #(.trigger("falling"), .width(4)) register_15 (
    .D(in_1), .en(demultiplexer_1_out13), .clk(clock_1_out), .Q(register_15_q), .clr(rst));
  Register #(.trigger("falling"), .width(4)) register_16 (
    .D(in_1), .en(demultiplexer_1_out15), .clk(clock_1_out), .Q(register_16_q), .clr(rst));
  Multiplexer #(.enable("true"), .select(4), .width(4)) multiplexer_1 (
    .in0(register_1_q), .in1(register_9_q), .in2(register_2_q), .in3(register_10_q), .in4(register_3_q),
    .in5(register_11_q), .in6(register_4_q), .in7(register_12_q), .in8(register_5_q), .in9(register_13_q),
    .in10(register_6_q), .in11(register_14_q), .in12(register_7_q), .in13(register_15_q),
    .in14(register_8_q), .in15(register_16_q), .out(out_7), .sel(in_5), .en(not_1_out));
  Multiplexer #(.enable("true"), .select(4), .width(4)) multiplexer_2 (
    .in0(register_1_q), .in1(register_9_q), .in2(register_2_q), .in3(register_10_q), .in4(register_3_q),
    .in5(register_11_q), .in6(register_4_q), .in7(register_12_q), .in8(register_5_q), .in9(register_13_q),
    .in10(register_6_q), .in11(register_14_q), .in12(register_7_q), .in13(register_15_q),
    .in14(register_8_q), .in15(register_16_q), .out(out_8), .sel(in_6), .en(not_1_out));

  // Notes on the sheet:
  //   wdata
  //   clk
  //   waddr
  //   rddr1
  //   rddr2
  //   rddr2
  //   rdata2
endmodule
