// Logisim project 1.circ as structural Verilog: 1 circuit, main circuit main
module main (
  input  [7:0] in_1,
  output out_2,
  output [7:0] out_3
);

  wire A, ADD, and_1_out, and_2_out, and_3_out, and_4_out, and_5_out, B, CLR, LDA, LDB, not_2_out, not_3_out,
       not_4_out, not_5_out, not_6_out, or_2_out, or_3_out, OVERFLOW, T1, T2;
  wire [7:0] controlled_buffer_1_out, register_2_q, register_3_q;

  and and_1 (and_1_out, ADD, T2);
  Register #(.width(1)) register_1 (.D(OVERFLOW), .clk(and_1_out), .Q(out_2), .clr(CLR));  // open: en
  and and_2 (and_2_out, LDA, T2);
  Register register_2 (.D(in_1), .clk(and_2_out), .Q(register_2_q), .clr(CLR));  // open: en
  Register register_3 (.D(out_3), .clk(and_3_out), .Q(register_3_q), .clr(CLR));  // open: en
  and and_3 (and_3_out, T2, LDB);
  assign controlled_buffer_1_out = ADD ? register_3_q : 8'bz;  // Controlled_Buffer controlled_buffer_1
  Adder adder_1 (.a(register_2_q), .b(controlled_buffer_1_out), .out(out_3), .cout(OVERFLOW));  // open: cin
  Clock clock_1 (.out(T1));
  not not_1 (T2, T1);
  or or_1 (LDA, and_4_out, and_5_out);
  and and_4 (and_4_out, not_2_out, not_3_out);
  not not_2 (not_2_out, A);
  not not_3 (not_3_out, B);
  and and_5 (and_5_out, A, B);
  or or_2 (or_2_out, A, B);
  D_Flip_Flop d_ff_1 (.D(or_2_out), .clk(T1), .Q(B));  // open: Qn, preset, reset
  xor xor_1 (LDB, A, B);
  and and_6 (ADD, not_4_out, B);
  not not_4 (not_4_out, A);
  not not_5 (not_5_out, A);
  D_Flip_Flop d_ff_2 (.D(or_3_out), .clk(T1), .Q(A));  // open: Qn, preset, reset
  or or_3 (or_3_out, not_5_out, not_6_out);
  not not_6 (not_6_out, B);
  nor nor_1 (CLR, A, B);
endmodule
