// Logisim project 定序型控制器-比较器.circ as structural Verilog: 1 circuit, main circuit main
module main (
  input  [7:0] in_1,
  output RESULT
);

  wire and_1_out, and_2_out, CAP, clock_1_out, CLR, LDA, LDB, nor_1_out, not_1_out, or_2_out, or_3_out, QA,
       QC;
  wire [7:0] controlled_buffer_1_out, controlled_buffer_2_out, register_1_q, register_2_q;

  or or_1 (LDB, QA, QC);
  Register register_1 (.Q(register_1_q), .clk(LDA), .clr(CLR));  // open: D, en
  Register register_2 (.D(in_1), .Q(register_2_q), .clk(LDB), .clr(CLR));  // open: en
  assign controlled_buffer_1_out = CAP ? register_1_q : 8'bz;  // Controlled_Buffer controlled_buffer_1
  assign controlled_buffer_2_out = CAP ? register_2_q : 8'bz;  // Controlled_Buffer controlled_buffer_2
  Clock clock_1 (.out(clock_1_out));
  Comparator comparator_1 (.a(controlled_buffer_1_out), .b(controlled_buffer_2_out), .gt(RESULT));  // open: eq, lt
  nor nor_1 (nor_1_out, QA, LDA, QC, CAP);
  D_Flip_Flop d_ff_1 (.clk(clock_1_out), .D(nor_1_out), .Q(QA));  // open: Qn, preset, en, reset
  or or_2 (or_2_out, QA, and_1_out);
  and and_1 (and_1_out, CAP, not_1_out);
  not not_1 (not_1_out, RESULT);
  D_Flip_Flop d_ff_2 (.clk(clock_1_out), .D(or_2_out), .Q(LDA));  // open: Qn, preset, en, reset
  or or_3 (or_3_out, LDA, and_2_out);
  and and_2 (and_2_out, CAP, RESULT);
  D_Flip_Flop d_ff_3 (.clk(clock_1_out), .D(or_3_out), .Q(QC));  // open: Qn, preset, en, reset
  D_Flip_Flop d_ff_4 (.clk(clock_1_out), .D(QC), .Q(CAP));  // open: Qn, preset, en, reset

  // Other names for the same wires on the sheet: A_B = RESULT; QB = LDA; QD = CAP
endmodule
