// Logisim project 多路选择器型_比较器.circ as structural Verilog: 1 circuit, main circuit main
module main (
  input  [7:0] in_1,
  input  in_2,
  input  in_3,
  output Result
);

  wire A, B, CAP, clock_1_out, CLR, LDA, LDB, multiplexer_1_out, multiplexer_2_out, not_1_out, not_2_out,
       not_3_out, not_5_out;
  wire [7:0] controlled_buffer_1_out, controlled_buffer_2_out, register_1_q, register_2_q;

  Clock clock_1 (.out(clock_1_out));
  not not_1 (not_1_out, in_2);
  Multiplexer #(.select(2)) multiplexer_1 (
    .in0(in_2), .in1(not_1_out), .in2(not_1_out), .in3(Result), .out(multiplexer_1_out), .sel({B, A}));  // open: en
  D_Flip_Flop d_ff_1 (.clk(clock_1_out), .D(multiplexer_1_out), .Q(B));  // open: Qn, preset, en, reset
  Register register_1 (.D(register_2_q), .Q(register_1_q), .clk(LDA), .clr(CLR));  // open: en
  Register register_2 (.D(in_1), .Q(register_2_q), .clk(LDB), .clr(CLR));  // open: en
  not not_2 (not_2_out, in_3);
  not not_3 (not_3_out, Result);
  assign controlled_buffer_1_out = CAP ? register_1_q : 8'bz;  // Controlled_Buffer controlled_buffer_1
  assign controlled_buffer_2_out = CAP ? register_2_q : 8'bz;  // Controlled_Buffer controlled_buffer_2
  Multiplexer #(.select(2)) multiplexer_2 (
    .in0(not_2_out), .in1(in_3), .in2(not_2_out), .in3(not_3_out), .out(multiplexer_2_out), .sel({B, A}));  // open: en
  D_Flip_Flop d_ff_2 (.clk(clock_1_out), .D(multiplexer_2_out), .Q(A));  // open: Qn, preset, en, reset
  Comparator comparator_1 (.a(controlled_buffer_1_out), .b(controlled_buffer_2_out), .gt(Result));  // open: eq, lt
  not not_4 (LDB, A);
  not not_5 (not_5_out, B);
  and and_1 (LDA, not_5_out, A);
  and and_2 (CAP, A, B);
  and and_3 (CLR, not_5_out, LDB);

  // Other names for the same wires on the sheet: A_B = Result

  // Notes on the sheet:
  //   RA
  //   RB
endmodule
