// Logisim project 计数器型-加法器.circ as structural Verilog: 1 circuit, main circuit main
module main (
  input  [7:0] in_1,
  output out_2,
  output [7:0] out_3
);

  wire A, ADD, and_1_out, and_2_out, and_3_out, and_4_out, and_5_out, B, CLR, LDA, LDB, not_1_out, not_2_out,
       not_4_out, not_5_out, not_6_out, or_2_out, or_3_out, OVERFLOW, T1, T2;
  wire [7:0] controlled_buffer_1_out, register_2_q, register_3_q;

  and and_1 (and_1_out, ADD, T2);
  Register #(.width(1)) register_1 (.D(OVERFLOW), .Q(out_2), .clk(and_1_out), .clr(CLR));  // open: en
  and and_2 (and_2_out, LDA, T2);
  Register register_2 (.D(in_1), .Q(register_2_q), .clk(and_2_out), .clr(CLR));  // open: en
  and and_3 (and_3_out, T2, LDB);
  assign controlled_buffer_1_out = ADD ? register_3_q : 8'bz;  // Controlled_Buffer controlled_buffer_1
  Register register_3 (.D(out_3), .Q(register_3_q), .clk(and_3_out), .clr(CLR));  // open: en
  Adder adder_1 (.a(register_2_q), .b(controlled_buffer_1_out), .out(out_3), .cout(OVERFLOW));  // open: cin
  Clock clock_1 (.out(T1));
  or or_1 (LDA, and_4_out, and_5_out);
  and and_4 (and_4_out, not_1_out, not_2_out);
  not not_1 (not_1_out, A);
  not not_2 (not_2_out, B);
  not not_3 (T2, T1);
  and and_5 (and_5_out, A, B);
  or or_2 (or_2_out, A, B);
  xor xor_1 (LDB, A, B);
  D_Flip_Flop d_ff_1 (.clk(T1), .D(or_2_out), .Q(B));  // open: Qn, preset, en, reset
  and and_6 (ADD, not_4_out, B);
  not not_4 (not_4_out, A);
  or or_3 (or_3_out, not_6_out, not_5_out);
  not not_5 (not_5_out, B);
  not not_6 (not_6_out, A);
  nor nor_1 (CLR, A, B);
  D_Flip_Flop d_ff_2 (.clk(T1), .D(or_3_out), .Q(A));  // open: Qn, preset, en, reset
endmodule
