// Logisim project 计数器型-比较器.circ as structural Verilog: 1 circuit, main circuit main
module main (
  input  [7:0] in_1,
  output Result
);

  wire A, and_4_out, and_5_out, B, CAP, clock_1_out, CLR, LDA, LDB, not_2_out, not_3_out, not_4_out,
       or_1_out, or_2_out, xor_1_out;
  wire [7:0] controlled_buffer_1_out, controlled_buffer_2_out, register_1_q, register_2_q;

  not not_1 (LDB, A);
  not not_2 (not_2_out, B);
  and and_1 (LDA, not_2_out, A);
  and and_2 (CAP, A, B);
  and and_3 (CLR, not_2_out, LDB);
  Register register_1 (.D(register_2_q), .Q(register_1_q), .clk(LDA), .clr(CLR));  // open: en
  Register register_2 (.D(in_1), .Q(register_2_q), .clk(LDB), .clr(CLR));  // open: en
  assign controlled_buffer_1_out = CAP ? register_1_q : 8'bz;  // Controlled_Buffer controlled_buffer_1
  assign controlled_buffer_2_out = CAP ? register_2_q : 8'bz;  // Controlled_Buffer controlled_buffer_2
  Clock clock_1 (.out(clock_1_out));
  xor xor_1 (xor_1_out, B, A);
  or or_1 (or_1_out, xor_1_out, and_4_out);
  and and_4 (and_4_out, B, Result);
  Comparator comparator_1 (.a(controlled_buffer_1_out), .b(controlled_buffer_2_out), .gt(Result));  // open: eq, lt
  D_Flip_Flop d_ff_1 (.clk(clock_1_out), .D(or_1_out), .Q(B));  // open: Qn, preset, en, reset
  not not_3 (not_3_out, A);
  or or_2 (or_2_out, not_3_out, and_5_out);
  and and_5 (and_5_out, B, not_4_out);
  not not_4 (not_4_out, Result);
  D_Flip_Flop d_ff_2 (.clk(clock_1_out), .D(or_2_out), .Q(A));  // open: Qn, preset, en, reset

  // Other names for the same wires on the sheet: A_B = Result
endmodule
